// Logisim project temp_run.circ as structural Verilog: 10 circuits, main circuit main
module main (
  output [15:0] Sum,
  output Overflow,
  output Underflow
);

  wire Adder_sign, ExpComp_se, Normalizer_overflow, Normalizer_underflow, PostRoundNorm_overflow,
       PostRoundNorm_underflow, Rounding_carry, Unpack_2_out_2, Unpack_out_2;
  wire [4:0] ExpComp_dele, ExpComp_e, Normalizer_e_norm_final, PostRoundNorm_e_final, Unpack_2_out_3,
       Unpack_out_3;
  wire [9:0] multiplexer_1_out, PostRoundNorm_m_final, Unpack_2_out_4, Unpack_out_4;
  wire [10:0] Rounding_sum;
  wire [13:0] GRS_out_2;
  wire [22:0] Shift_a, Shift_a_2;
  wire [23:0] Adder_sum, Normalizer_m_norm_final;

  Unpack Unpack (.in_1(16'hb400), .out_2(Unpack_out_2), .out_3(Unpack_out_3), .out_4(Unpack_out_4));
  Unpack Unpack_2 (.in_1(16'hb400), .out_2(Unpack_2_out_2), .out_3(Unpack_2_out_3), .out_4(Unpack_2_out_4));
  ExpComp ExpComp (.EA(Unpack_out_3), .EB(Unpack_2_out_3), .E(ExpComp_e), .delE(ExpComp_dele), .SE(ExpComp_se));
  AdderShifter Shift (
    .delE(ExpComp_dele), .SE(ExpComp_se), .MA(Unpack_out_4), .MA_2(Unpack_2_out_4), .A(Shift_a),
    .A_2(Shift_a_2));
  MantissaAdder Adder (
    .SA(Unpack_out_2), .MA(Shift_a), .SB(Unpack_2_out_2), .MB(Shift_a_2), .Sign(Adder_sign), .Sum(Adder_sum));
  Normalizer Normalizer (
    .M(Adder_sum), .E(ExpComp_e), .M_NORM_FINAL(Normalizer_m_norm_final),
    .E_NORM_FINAL(Normalizer_e_norm_final), .OVERFLOW(Normalizer_overflow), .UNDERFLOW(Normalizer_underflow));
  GRS GRS (.in_1(Normalizer_m_norm_final), .out_2(GRS_out_2));
  Round Rounding (.L(GRS_out_2), .SUM(Rounding_sum), .CARRY(Rounding_carry));
  PostRoundNorm PostRoundNorm (
    .SUM(Rounding_sum), .CARRY(Rounding_carry), .E(Normalizer_e_norm_final), .M_FINAL(PostRoundNorm_m_final),
    .E_FINAL(PostRoundNorm_e_final), .OVERFLOW(PostRoundNorm_overflow), .UNDERFLOW(PostRoundNorm_underflow));
  Pack Pack (.in_1(Adder_sign), .in_2(PostRoundNorm_e_final), .in_3(multiplexer_1_out), .out_4(Sum));
  Multiplexer #(.width(10), .enable("false")) multiplexer_1 (
    .in0(PostRoundNorm_m_final), .in1({10{1'b0}}), .out(multiplexer_1_out), .sel(Overflow));
  or or_1 (Overflow, PostRoundNorm_overflow, Normalizer_overflow);
  and and_1 (Underflow, PostRoundNorm_underflow, Normalizer_underflow);
endmodule

module Unpack (
  input  [15:0] in_1,
  output out_2,
  output [4:0] out_3,
  output [9:0] out_4
);


  assign out_2 = in_1[15];
  assign out_3 = in_1[14:10];
  assign out_4 = in_1[9:0];
endmodule

module AdderShifter (
  input  [4:0] delE,
  input  SE,
  input  [9:0] MA,
  input  [9:0] MA_2,
  output [22:0] A,
  output [22:0] A_2
);

  wire [4:0] demultiplexer_1_out0, demultiplexer_1_out1;
  wire [10:0] and_1_out, and_2_out, bit_extender_1_out, bit_extender_2_out;
  wire [21:0] bit_extender_3_out, bit_extender_4_out, shifter_1_out, shifter_2_out, shifter_3_out,
       shifter_4_out;

  assign bit_extender_1_out = {{1{1'b1}}, MA};  // Bit_Extender bit_extender_1
  assign bit_extender_2_out = {{1{1'b1}}, MA_2};  // Bit_Extender bit_extender_2
  assign bit_extender_3_out = {{11{1'b0}}, bit_extender_1_out};  // Bit_Extender bit_extender_3
  assign bit_extender_4_out = {{11{1'b0}}, bit_extender_2_out};  // Bit_Extender bit_extender_4
  Demultiplexer #(.width(5), .enable("false")) demultiplexer_1 (
    .out0(demultiplexer_1_out0), .out1(demultiplexer_1_out1), .in(delE), .sel(SE));
  Shifter #(.width(22)) shifter_1 (.in(bit_extender_3_out), .\dist (5'b01011), .out(shifter_1_out));
  Shifter #(.width(22)) shifter_2 (.in(bit_extender_4_out), .\dist (5'b01011), .out(shifter_2_out));
  Shifter #(.width(22)) shifter_3 (.in({22{1'b1}}), .\dist (demultiplexer_1_out0), .out(shifter_3_out));
  Shifter #(.width(22)) shifter_4 (.in({22{1'b1}}), .\dist (demultiplexer_1_out1), .out(shifter_4_out));
  Shifter #(.width(22), .shift("lr")) shifter_5 (.in(shifter_1_out), .\dist (demultiplexer_1_out0), .out(A[22:1]));
  assign and_1_out = bit_extender_1_out & ~shifter_3_out[21:11];  // AND_Gate and_1, 11 bits wide
  Shifter #(.width(22), .shift("lr")) shifter_6 (.in(shifter_2_out), .\dist (demultiplexer_1_out1), .out(A_2[22:1]));
  assign and_2_out = bit_extender_2_out & ~shifter_4_out[21:11];  // AND_Gate and_2, 11 bits wide
  or or_1 (A[0], and_1_out[0], and_1_out[1], and_1_out[2], and_1_out[3], and_1_out[4], and_1_out[5], and_1_out[6], and_1_out[7], and_1_out[8], and_1_out[9], and_1_out[10]);
  or or_2 (A_2[0], and_2_out[0], and_2_out[1], and_2_out[2], and_2_out[3], and_2_out[4], and_2_out[5], and_2_out[6], and_2_out[7], and_2_out[8], and_2_out[9], and_2_out[10]);
endmodule

module ExpComp (
  input  [4:0] EA,
  input  [4:0] EB,
  output [4:0] E,
  output [4:0] delE,
  output SE
);

  wire comparator_1_lt;
  wire [5:0] negator_1_out, subtractor_1_out;
  wire [5:5] multiplexer_2_out;

  Subtractor #(.width(6)) subtractor_1 (.a({1'b0, EA}), .b({1'b0, EB}), .out(subtractor_1_out));  // open: bin, bout
  Negator #(.width(6)) negator_1 (.in(subtractor_1_out), .out(negator_1_out));
  Multiplexer #(.width(5), .enable("false")) multiplexer_1 (.in0(EA), .in1(EB), .out(E), .sel(comparator_1_lt));
  Comparator #(.width(5), .mode("unsigned")) comparator_1 (.a(EA), .b(EB), .gt(SE), .lt(comparator_1_lt));  // open: eq
  Multiplexer #(.width(6), .enable("false")) multiplexer_2 (
    .in0(subtractor_1_out), .in1(negator_1_out), .out({multiplexer_2_out[5], delE}), .sel(comparator_1_lt));
endmodule

module MantissaAdder (
  input  SA,
  input  [22:0] MA,
  input  SB,
  input  [22:0] MB,
  output Sign,
  output [23:0] Sum
);

  wire [23:0] adder_1_out, negator_3_out;
  wire [24:0] bit_extender_1_out, bit_extender_2_out, multiplexer_1_out, multiplexer_2_out, negator_1_out,
       negator_2_out;

  assign bit_extender_1_out = {{2{1'b0}}, MA};  // Bit_Extender bit_extender_1
  assign bit_extender_2_out = {{2{1'b0}}, MB};  // Bit_Extender bit_extender_2
  Multiplexer #(.width(25), .enable("false")) multiplexer_1 (
    .in0(bit_extender_1_out), .in1(negator_1_out), .out(multiplexer_1_out), .sel(SA));
  Negator #(.width(25)) negator_1 (.in(bit_extender_1_out), .out(negator_1_out));
  Multiplexer #(.width(25), .enable("false")) multiplexer_2 (
    .in0(bit_extender_2_out), .in1(negator_2_out), .out(multiplexer_2_out), .sel(SB));
  Negator #(.width(25)) negator_2 (.in(bit_extender_2_out), .out(negator_2_out));
  Adder #(.width(25)) adder_1 (
    .a(multiplexer_1_out), .b(multiplexer_2_out), .out({Sign, adder_1_out}));  // open: cin, cout
  Negator #(.width(24)) negator_3 (.in(adder_1_out), .out(negator_3_out));
  Multiplexer #(.width(24), .enable("false")) multiplexer_3 (
    .in0(adder_1_out), .in1(negator_3_out), .out(Sum), .sel(Sign));
endmodule

module Normalizer (
  input  [23:0] M,
  input  [4:0] E,
  output [23:0] M_NORM_FINAL,
  output [4:0] E_NORM_FINAL,
  output OVERFLOW,
  output UNDERFLOW
);

  wire and_1_out, and_2_out, comparator_1_lt, EXP_ZERO_out, leftt_select_out, not_1_out, or_2_out, or_3_out,
       priority_encoder_1_en_out;
  wire [4:0] adder_1_out, adder_2_out, multiplexer_2_out, multiplexer_4_out, multiplexer_5_out,
       pull_resistor_1_node, subtractor_1_out, subtractor_2_out, subtractor_3_out;
  wire [23:0] multiplexer_1_out, multiplexer_3_out, shifter_1_out, shifter_2_out;

  and leftt_select (leftt_select_out, ~priority_encoder_1_en_out, ~M[23]);  // AND_Gate
  Shifter #(.width(24), .shift("lr")) shifter_1 (.in(M), .\dist (5'b00001), .out(shifter_1_out));
  Adder #(.width(5)) adder_1 (.a(E), .b(5'b00001), .out(adder_1_out));  // open: cin, cout
  Pull_Resistor pull_resistor_1 (.node(pull_resistor_1_node));
  Priority_Encoder #(.select(5), .disabled(0)) priority_encoder_1 (
    .in0(M[0]), .in1(M[1]), .in2(M[2]), .in3(M[3]), .in4(M[4]), .in5(M[5]), .in6(M[6]), .in7(M[7]),
    .in8(M[8]), .in9(M[9]), .in10(M[10]), .in11(M[11]), .in12(M[12]), .in13(M[13]), .in14(M[14]),
    .in15(M[15]), .in16(M[16]), .in17(M[17]), .in18(M[18]), .in19(M[19]), .in20(M[20]), .in21(M[21]),
    .in22(M[22]), .out(pull_resistor_1_node), .en_out(priority_encoder_1_en_out), .en_in(1'b1));  // open: in23, in24, in25, in26, in27, in28, in29, in30, in31, gs
  Subtractor #(.width(5)) subtractor_1 (
    .a(5'b10110), .b(pull_resistor_1_node), .out(subtractor_1_out));  // open: bin, bout
  Multiplexer #(.width(24), .enable("false")) multiplexer_1 (
    .in0(M), .in1(shifter_1_out), .out(multiplexer_1_out), .sel(M[23]));
  Multiplexer #(.width(5), .enable("false")) multiplexer_2 (
    .in0(E), .in1(adder_1_out), .out(multiplexer_2_out), .sel(M[23]));
  Shifter #(.width(24)) shifter_2 (.in(M), .\dist (subtractor_1_out), .out(shifter_2_out));
  Subtractor #(.width(5)) subtractor_2 (.a(E), .b(subtractor_1_out), .out(subtractor_2_out));  // open: bin, bout
  Comparator #(.width(5), .mode("unsigned")) comparator_1 (
    .a(E), .b(subtractor_1_out), .lt(comparator_1_lt));  // open: gt, eq
  Adder #(.width(5)) adder_2 (.a(5'b00001), .b(subtractor_3_out), .out(adder_2_out));  // open: cin, cout
  Subtractor #(.width(5)) subtractor_3 (.a(subtractor_1_out), .b(E), .out(subtractor_3_out));  // open: bin, bout
  Multiplexer #(.width(24), .enable("false")) multiplexer_3 (
    .in0(multiplexer_1_out), .in1(shifter_2_out), .out(multiplexer_3_out), .sel(leftt_select_out));
  Multiplexer #(.width(5), .enable("false")) multiplexer_4 (
    .in0(multiplexer_2_out), .in1(subtractor_2_out), .out(multiplexer_4_out), .sel(leftt_select_out));
  Multiplexer #(.width(5), .enable("false")) multiplexer_5 (
    .in0({5{1'b0}}), .in1(adder_2_out), .out(multiplexer_5_out), .sel(or_2_out));
  and and_1 (and_1_out, comparator_1_lt, leftt_select_out);
  Shifter #(.width(24), .shift("lr")) shifter_3 (
    .in(multiplexer_3_out), .\dist (multiplexer_5_out), .out(M_NORM_FINAL));
  and and_2 (and_2_out, multiplexer_4_out[0], multiplexer_4_out[1], multiplexer_4_out[2], multiplexer_4_out[3], multiplexer_4_out[4]);
  nor EXP_ZERO (EXP_ZERO_out, multiplexer_4_out[0], multiplexer_4_out[1], multiplexer_4_out[2], multiplexer_4_out[3], multiplexer_4_out[4]);
  Multiplexer #(.width(5), .enable("false")) multiplexer_6 (
    .in0(multiplexer_4_out), .in1({5{1'b0}}), .out(E_NORM_FINAL), .sel(UNDERFLOW));
  or or_1 (UNDERFLOW, or_2_out, not_1_out);
  and and_3 (OVERFLOW, and_2_out, ~or_2_out);  // AND_Gate
  or or_2 (or_2_out, EXP_ZERO_out, and_1_out);
  or or_3 (or_3_out, multiplexer_3_out[0], multiplexer_3_out[1], multiplexer_3_out[2], multiplexer_3_out[3], multiplexer_3_out[4], multiplexer_3_out[5], multiplexer_3_out[6], multiplexer_3_out[7], multiplexer_3_out[8], multiplexer_3_out[9], multiplexer_3_out[10], multiplexer_3_out[11], multiplexer_3_out[12], multiplexer_3_out[13], multiplexer_3_out[14], multiplexer_3_out[15], multiplexer_3_out[16], multiplexer_3_out[17], multiplexer_3_out[18], multiplexer_3_out[19], multiplexer_3_out[20], multiplexer_3_out[21], multiplexer_3_out[22], multiplexer_3_out[23], multiplexer_3_out[23]);
  not not_1 (not_1_out, or_3_out);
endmodule

module GRS (
  input  [23:0] in_1,
  output [13:0] out_2
);

  or or_1 (out_2[0], in_1[0], in_1[1], in_1[2], in_1[3], in_1[4], in_1[5], in_1[6], in_1[7], in_1[8], in_1[9], in_1[9]);

  assign out_2[13:1] = in_1[22:10];
endmodule

module Round (
  input  [13:0] L,
  output [10:0] SUM,
  output CARRY
);

  wire R_S_F0_out, Round_Up_out;

  or R_S_F0 (R_S_F0_out, L[3], L[1], L[0]);
  and Round_Up (Round_Up_out, R_S_F0_out, L[2]);
  Adder #(.width(11)) adder_1 (.a(L[13:3]), .b({11{1'b0}}), .out(SUM), .cin(Round_Up_out), .cout(CARRY));
endmodule

module PostRoundNorm (
  input  [10:0] SUM,
  input  CARRY,
  input  [4:0] E,
  output [9:0] M_FINAL,
  output [4:0] E_FINAL,
  output OVERFLOW,
  output UNDERFLOW
);

  Adder #(.width(5)) adder_1 (.a(E), .b({5{1'b0}}), .out(E_FINAL), .cin(CARRY));  // open: cout
  and Sum_E_bits (OVERFLOW, E_FINAL[0], E_FINAL[1], E_FINAL[2], E_FINAL[3], E_FINAL[4]);
  nor for_underflow (UNDERFLOW, E_FINAL[0], E_FINAL[1], E_FINAL[2], E_FINAL[3], E_FINAL[4]);

  assign M_FINAL = SUM[9:0];
endmodule

module Pack (
  input  in_1,
  input  [4:0] in_2,
  input  [9:0] in_3,
  output [15:0] out_4
);


  assign out_4 = {in_1, in_2, in_3};
endmodule
